// Logisim project projet.circ as structural Verilog: 3 circuits, main circuit main
module main (
  input  [7:0] Input,
  input  \E__1_activé_0_desac ,
  input  \Code_opé_0_dépiler_1_empiler ,
  input  Clear,
  output \Débordement ,
  output [7:0] Output
);

  wire [7:0] Pile_output;

  Pile Pile (
    .Input(Input), .E(\E__1_activé_0_desac ), .\Code_opé (\Code_opé_0_dépiler_1_empiler ), .Clear(Clear),
    .Output(Pile_output));
  \Unité_de_calcul  Unit_calcul ();  // open: A, B, Code_opé, D, S

  // Notes on the sheet:
  //   Bit poids fort
endmodule

module \Unité_de_calcul  (
  input  [7:0] A,
  input  [7:0] B,
  input  [1:0] \Code_opé ,
  output D,
  output [7:0] S
);

  wire adder_1_cout, comparator_1_eq, comparator_2_eq, not_1_out;
  wire [3:0] multiplier_2_out;
  wire [7:0] adder_1_out, divider_1_out, multiplier_1_out, subtractor_1_out;

  Adder adder_1 (.a(A), .b(B), .out(adder_1_out), .cout(adder_1_cout));  // open: cin
  Subtractor subtractor_1 (.a(A), .b(B), .out(subtractor_1_out));  // open: bin, bout
  Multiplier multiplier_1 (.a(A), .b(B), .out(multiplier_1_out));  // open: cin, cout
  Divider divider_1 (.a(A), .b(B), .out(divider_1_out));  // open: upper, rem
  Multiplier #(.width(4)) multiplier_2 (.a(A[7:4]), .b(B[7:4]), .out(multiplier_2_out));  // open: cin, cout
  Comparator comparator_1 (.a(B), .b({8{1'b0}}), .eq(comparator_1_eq));  // open: gt, lt
  Comparator #(.width(4)) comparator_2 (.a(multiplier_2_out), .b(4'b0000), .eq(comparator_2_eq));  // open: gt, lt
  not not_1 (not_1_out, comparator_2_eq);
  Multiplexer #(.select(2), .width(8)) multiplexer_1 (
    .in0(adder_1_out), .in1(subtractor_1_out), .in2(multiplier_1_out), .in3(divider_1_out), .out(S),
    .sel(\Code_opé ), .en(1'b1));
  Multiplexer #(.select(2)) multiplexer_2 (
    .in0(adder_1_cout), .in1(1'b0), .in2(not_1_out), .in3(comparator_1_eq), .out(D), .sel(\Code_opé ),
    .en(1'b1));

  // Notes on the sheet:
  //   Overflow impossible
  //   with 2 unsigned int
  //   Result *
  //   Overflow *
  //   Result +
  //   Overflow +
  //   Result /
  //   Overflow /
  //   Result -
  //   S : sortie du calcul
  //   A, B : Paramètres du calcul
  //   D : Indication si le résultat a débordé
  //   Code opé : Code d'opération (00+, 01-, 10*, 11/)
endmodule

module Pile (
  input  [7:0] Input,
  input  E,
  input  \Code_opé ,
  input  Clear,
  output [7:0] Output
);

  wire and_1_out, CLK_out, counter_1_carry, not_1_out, not_2_out, not_3_out;
  wire [7:0] counter_1_q;

  not not_1 (not_1_out, \Code_opé );
  Counter counter_1 (
    .load(not_1_out), .count(1'b1), .Q(counter_1_q), .carry(counter_1_carry), .clk(CLK_out), .clr(Clear));  // open: D
  not not_2 (not_2_out, counter_1_carry);
  Clock CLK (.out(CLK_out));
  and and_1 (and_1_out, not_2_out, E);
  not not_3 (not_3_out, \Code_opé );
  RAM #(.bus("separate")) ram_1 (
    .addr(counter_1_q), .din(Input), .data(Output), .str(\Code_opé ), .sel(and_1_out), .clk(CLK_out),
    .ld(not_3_out), .clr(Clear));

  // Notes on the sheet:
  //   E : si E = 0, la pile conserve le contenu, sinon elle réalise une opération
  //   Input : Entrée de données
  //   Output : Sortie de données
  //   Code opé : 0 dépiler, 1 empiler
endmodule
